# Fritzing sketch info_bot (saved by Fritzing 0.9.2b)
breadboards: 1

parts:
  Part1 = Photon
  U1 = LCD-16X2 [package=lcd-16x2]
  R1 = TRIMPOT [package=trimpot_tc33]
  S1 = Momentary Switch [package=tactile_switch_smd]
  R2 = Resistor [tolerance=±5% resistance=10k package="0805 [SMD]"]

nets:
  N1: Part1.A4, S1.1
  GND: Part1.GND, U1.VSS, U1.R_W, U1.K, R1.WIPER, R2.Pin_1
  VIN: Part1.VIN, U1.VDD, U1.A, S1.3
  N2: Part1.D0, U1.RS
  N3: Part1.D1, U1.E
  N4: Part1.D2, U1.DB4
  N5: Part1.D3, U1.DB5
  N6: Part1.D4, U1.DB6
  N7: Part1.D5, U1.DB7
  N8: Part1.3V3, R1.CCW
  N9: U1.VO, R1.CW
  N10: S1.4, R2.Pin_0
